# Fritzing sketch CANtempSensor (saved by Fritzing 0.9.4)
breadboards: 1

parts:
  M2 = Niren can bus module [package=THT]
  IC1 = IC, DIP package, 16 pins [chip_label=ADUM5401]
  Part1 = Arduino Nano (Rev3.0)
  U1 = MAX6675 [package=so08]
  JP2 = Header 4 [package=1x04-1mm-ra]
  C1 = Capacitor [package=cap-pth-large]
  C2 = Capacitor [package=cap-pth-large]
  J1 = Peltier Element

nets (from the schematic view):
  N1: M2.pin1, Part1.5V, JP2.1
  GND: M2.pin2, JP2.2
  N2: M2.pin3, Part1.D10
  N3: M2.pin4, Part1.D12/MISO
  N4: M2.pin5, Part1.D11/MOSI
  N5: M2.pin6, Part1.D13/SCK
  N6: M2.pin12, JP2.4
  N7: M2.pin13, JP2.3
  N8: IC1.pin1, C1.1
  N9: IC1.pin2, IC1.pin7, C1.2
  N10: IC1.pin4, Part1.D5
  N11: IC1.pin5, Part1.D6
  N12: IC1.pin6, Part1.D4
  N13: IC1.pin10, IC1.pin15, U1.VSS, C2.2
  N14: IC1.pin11, U1.MISO
  N15: IC1.pin12, U1.SCK
  N16: IC1.pin13, U1.CS
  N17: IC1.pin16, U1.VDD, C2.1
  N18: U1.T-, J1.pin2
  N19: U1.T+, J1.pin1

custom parts:
  Niren can bus module: Niren can bus module availabe on ebay and others. No pcb view as no mechanical drawng and it wouldn't mount anyway.
