# Fritzing sketch TemperatureCAN (saved by Fritzing 0.9.3b)
breadboards: 1

parts:
  Part1 = Arduino Nano (Rev3.0)
  M2 = Niren can bus module [package=THT]
  U1 = MAX6675 [package=so08]
  H1 = polarizedheader 4pin 0.156in [package=THT]

nets:
  N1: Part1.D4, U1.MISO
  N2: Part1.D5, U1.CS
  N3: Part1.D6, U1.SCK
  N4: Part1.D10, M2.pin3
  N5: Part1.D11/MOSI, M2.pin5
  N6: Part1.D12/MISO, M2.pin4
  N7: Part1.5V, M2.pin1, H1.pin1
  3V3: Part1.3V3, U1.VDD
  N8: Part1.D13/SCK, M2.pin6
  GND: M2.pin2, H1.pin2
  N9: M2.pin10, M2.pin12, H1.pin4
  N10: M2.pin11, M2.pin13, H1.pin3

custom parts:
  Niren can bus module: Niren can bus module availabe on ebay and others. No pcb view as no mechanical drawng and it wouldn't mount anyway.
